# Fritzing sketch Diagram (saved by Fritzing 0.9.3b)

parts:
  Деталь1 = FTDI Basic Programmer
  ESP32_-_Back1 = ESP32 - CAM
  S1 = Pushbutton [package=THT]

nets:
  N1: Деталь1.RXI, ESP32_-_Back1.GPIO1_/_TX
  N2: Деталь1.TXO, ESP32_-_Back1.GPIO3_/_RX
  N3: Деталь1.POWER, ESP32_-_Back1.5V
  N4: Деталь1.GND, ESP32_-_Back1.GND#7
  N5: ESP32_-_Back1.GPIO0, S1.leg1
  N6: ESP32_-_Back1.GND#16, S1.leg0

custom parts:
  ESP32 - CAM: The ESP32-CAM has a very competitive small-size camera module that can operate independently as a minimum system with a footprint of only 27*40.5*4.5mm and a deep sleep current of up to 6mA.
